# Fritzing sketch Diagrama_casa (saved by Fritzing 0.9.3b)
breadboards: 1

parts:
  Raspberry_Pi_1 = Raspberry Pi 3 [part_number=RPI-3-V1.2]
  Componente1 = Adafruit T-Cobbler Plus [part_number="Adafruit #1989 and #2028"]
  LED1 = LEDs [package=led10mm]
  LED2 = LEDs [package=led10mm]
  LED3 = LEDs [package=led10mm]
  LED4 = LEDs [package=led10mm]
  LED6 = LEDs [package=led10mm]
  LED7 = LEDs [package=led10mm]
  LED8 = LEDs [package=led10mm]
  LED9 = LEDs [package=led10mm]
  LED10 = LEDs [package=led10mm]
  LED11 = LEDs [package=led10mm]
  LED12 = LEDs [package=led10mm]
  J1 = Piezo Speaker
  J2 = Piezo Speaker
  J3 = Piezo Speaker
  R1 = PHOTOCELL [package=photocell]
  C1 = Electrolytic Capacitor [capacitance=100nF package="100 mil [THT, electrolytic]"]
  D1 = LTE-302 [package=lte-302]
  S1 = Toggle Switch [package=THT]
  PIR2 = PIR sensor

nets:
  3V3: Raspberry_Pi_1.3v3, Raspberry_Pi_1.3V3, Componente1.+3.3V, Componente1.+3.3V_2, R1.P$2
  N1: Raspberry_Pi_1.GPIO2, Componente1.SDA
  N2: Raspberry_Pi_1.GPIO3, Componente1.SCL
  N3: Raspberry_Pi_1.GIPO4, Componente1.GPIO4
  GND: Raspberry_Pi_1.GND, Componente1.GND, LED7.C, LED8.C, LED9.C, LED10.C, LED11.C, LED12.C, C1.-, D1.C, PIR2.GND
  N4: Raspberry_Pi_1.GIPO17, Componente1.GPIO17
  N5: Raspberry_Pi_1.GIPO27, Componente1.GPIO27, LED12.A
  N6: Raspberry_Pi_1.GIPO22, Componente1.GPIO22, PIR2.SIG
  N7: Raspberry_Pi_1.GIPO10, Componente1.MOSI
  N8: Raspberry_Pi_1.GIPO9, Componente1.MISO, LED8.A
  N9: Raspberry_Pi_1.GIPO11, Componente1.SCLK
  N10: Raspberry_Pi_1.ID_SD, Componente1.EEDAT
  N11: Raspberry_Pi_1.GIPO5, Componente1.GPIO5, LED9.A
  N12: Raspberry_Pi_1.GIPO6, Componente1.GPIO6, LED10.A
  N13: Raspberry_Pi_1.GIPO13, Componente1.GPIO13, LED7.A
  N14: Raspberry_Pi_1.GIPO19, Componente1.GPIO19, LED11.A
  N15: Raspberry_Pi_1.GIPO26, Componente1.GPIO26, D1.A
  N16: Raspberry_Pi_1.GIPO21, Componente1.GPIO21, LED1.A
  N17: Raspberry_Pi_1.GIPO20, Componente1.GPIO20, LED6.A
  N18: Raspberry_Pi_1.GIPO16, Componente1.GPIO16, S1.COM
  N19: Raspberry_Pi_1.GIPO12, Componente1.GPIO12, LED4.A
  N20: Raspberry_Pi_1.ID_SC, Componente1.EECLK
  N21: Raspberry_Pi_1.GIPO7, Componente1.CE1, LED3.A
  N22: Raspberry_Pi_1.GIPO8, Componente1.CE0, R1.P$1, C1.+
  N23: Raspberry_Pi_1.GIPO25, Componente1.GPIO25, LED2.A
  N24: Raspberry_Pi_1.GIPO24, Componente1.GPIO24, J3.pin2
  N25: Raspberry_Pi_1.GIPO23, Componente1.GPIO23
  N26: Raspberry_Pi_1.GIPO18, Componente1.GPIO18
  N27: Raspberry_Pi_1.GIPO15, Componente1.RXD, J2.pin2
  N28: Raspberry_Pi_1.GIPO14, Componente1.TXD, LED1.C, LED2.C, LED3.C, LED4.C, LED6.C, J1.pin1, J1.pin2, J2.pin1, J3.pin1, S1.L1
  5V: Raspberry_Pi_1.5V, Componente1.+5V, S1.L2, PIR2.VDD

custom parts:
  Adafruit T-Cobbler Plus: The Raspberry Pi has landed on the Maker World like a 40-GPIO pinned, quad-USB ported, credit card sized bomb of DIY joy. And while you can use most of our great Model B accessories by hooking up our downgrade cable, its probably a good time to upgrade your set up and accessorize using all of the 40 pins. That's why we now carry the Assembled Adafruit Pi T-Cobbler Plus - Breakout + Cable for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
